// Logisim project 1.5) Décodeur et Afficheur 7 segments.circ as structural Verilog: 1 circuit, main circuit main
module main (
  input  e0,
  input  e1,
  output s5,
  output s4,
  output s6,
  output s3,
  output s2,
  output s0,
  output s1
);

  wire not_1_out, not_2_out, not_3_out, not_5_out, not_6_out;

  not not_1 (not_1_out, e1);
  not not_2 (not_2_out, e0);
  not not_3 (not_3_out, e1);
  not not_4 (s2, e1);
  not not_5 (not_5_out, e0);
  not not_6 (not_6_out, e1);
  or or_1 (s5, not_1_out, e0);
  and and_1 (s4, not_2_out, not_3_out);
  or or_2 (s0, not_5_out, e1);
  or or_3 (s1, not_6_out, e0);

  assign s3 = e0;
  assign s6 = 1'b1;
endmodule
